# Fritzing sketch 6 DOF Robotic Arm (saved by Fritzing 1.0.5)

parts:
  A1 = XY-3606
  Raspberry_Pi_1 = Raspberry Pi 3 [part_number=RPI-3-V1.2]
  Part1 = Adafruit PCA9685 PWM/Servo Breakout [part_number=815]
  J1 = Basic Servo

nets:
  GND: A1.Pin_2, A1.Pin_3, Raspberry_Pi_1.GND, Part1.GND, J1.gnd
  N1: A1.Pin_4, Part1.PWRIN
  3V3: Raspberry_Pi_1.3v3, Raspberry_Pi_1.3V3, Part1.VCC
  N2: Raspberry_Pi_1.GPIO2, Part1.SDA
  N3: Raspberry_Pi_1.GPIO3, Part1.SCL
  N4: Part1.PWM4, J1.pulse
  N5: Part1.5.0V, J1.vcc

custom parts:
  XY-3606: 24V/12V turn 5V 5A power module, DC-DC XY-3606 Power Converter Super LM2596S.
  Adafruit PCA9685 PWM/Servo Breakout: Using only two pins, control 16 free-running PWM outputs! I2C-controlled PWM driver with a built in clock. Unlike the TLC5940 family, you do not need to continuously send it signal tying up your microcontroller, its completely free running! 5V compliant, which means you can control it from a 3.3V microcontroller and still safely drive up to 6V outputs (this is good for when you want to control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
